// Logisim project cpu_risc_v.circ as structural Verilog
module interger_register_file (
  input  Clock,
  input  EnableWrite,
  input  [3:0] ReadRegisterY,
  input  EnableRead,
  input  [3:0] ReadRegisterX,
  input  [3:0] SetRegister,
  input  [31:0] Data,
  output [31:0] OutputY,
  output [31:0] OutputX
);

  wire decoder_1_out0, decoder_1_out1, decoder_1_out2, decoder_1_out3, decoder_1_out4, decoder_1_out5,
       decoder_1_out6, decoder_1_out7, decoder_1_out8, decoder_1_out9, decoder_1_out10, decoder_1_out11,
       decoder_1_out12, decoder_1_out13, decoder_1_out14, decoder_1_out15, ER0_out, ER1_out, ER2_out,
       ER3_out, ER4_out, ER5_out, ER6_out, ER7_out, ER8_out, ER9_out, ER10_out, ER11_out, ER12_out, ER13_out,
       ER14_out, ER15_out;
  wire [31:0] demultiplexer_1_out0, demultiplexer_1_out1, demultiplexer_1_out2, demultiplexer_1_out3,
       demultiplexer_1_out4, demultiplexer_1_out5, demultiplexer_1_out6, demultiplexer_1_out7,
       demultiplexer_1_out8, demultiplexer_1_out9, demultiplexer_1_out10, demultiplexer_1_out11,
       demultiplexer_1_out12, demultiplexer_1_out13, demultiplexer_1_out14, demultiplexer_1_out15,
       register_1_q, register_2_q, register_3_q, register_4_q, register_5_q, register_6_q, register_7_q,
       register_8_q, register_9_q, register_10_q, register_11_q, register_12_q, register_13_q, register_14_q,
       register_15_q, register_16_q;

  Decoder #(.enable("false"), .select(4)) decoder_1 (
    .out0(decoder_1_out0), .out1(decoder_1_out1), .out2(decoder_1_out2), .out3(decoder_1_out3),
    .out4(decoder_1_out4), .out5(decoder_1_out5), .out6(decoder_1_out6), .out7(decoder_1_out7),
    .out8(decoder_1_out8), .out9(decoder_1_out9), .out10(decoder_1_out10), .out11(decoder_1_out11),
    .out12(decoder_1_out12), .out13(decoder_1_out13), .out14(decoder_1_out14), .out15(decoder_1_out15),
    .sel(SetRegister));
  and ER0 (ER0_out, EnableWrite, decoder_1_out0);
  and ER1 (ER1_out, EnableWrite, decoder_1_out1);
  and ER2 (ER2_out, EnableWrite, decoder_1_out2);
  and ER3 (ER3_out, EnableWrite, decoder_1_out3);
  and ER4 (ER4_out, EnableWrite, decoder_1_out4);
  and ER5 (ER5_out, EnableWrite, decoder_1_out5);
  and ER6 (ER6_out, EnableWrite, decoder_1_out6);
  and ER7 (ER7_out, EnableWrite, decoder_1_out7);
  and ER8 (ER8_out, EnableWrite, decoder_1_out8);
  and ER9 (ER9_out, EnableWrite, decoder_1_out9);
  and ER10 (ER10_out, EnableWrite, decoder_1_out10);
  and ER11 (ER11_out, EnableWrite, decoder_1_out11);
  and ER12 (ER12_out, EnableWrite, decoder_1_out12);
  and ER13 (ER13_out, EnableWrite, decoder_1_out13);
  and ER14 (ER14_out, EnableWrite, decoder_1_out14);
  and ER15 (ER15_out, EnableWrite, decoder_1_out15);
  Register #(.width(32)) register_1 (
    .D(demultiplexer_1_out0), .en(ER0_out), .Q(register_1_q), .clk(Clock));  // open: clr
  Register #(.width(32)) register_2 (
    .D(demultiplexer_1_out1), .en(ER1_out), .Q(register_2_q), .clk(Clock));  // open: clr
  Register #(.width(32)) register_3 (
    .D(demultiplexer_1_out2), .en(ER2_out), .Q(register_3_q), .clk(Clock));  // open: clr
  Register #(.width(32)) register_4 (
    .D(demultiplexer_1_out3), .en(ER3_out), .Q(register_4_q), .clk(Clock));  // open: clr
  Register #(.width(32)) register_5 (
    .D(demultiplexer_1_out4), .en(ER4_out), .Q(register_5_q), .clk(Clock));  // open: clr
  Register #(.width(32)) register_6 (
    .D(demultiplexer_1_out5), .en(ER5_out), .Q(register_6_q), .clk(Clock));  // open: clr
  Register #(.width(32)) register_7 (
    .D(demultiplexer_1_out6), .en(ER6_out), .Q(register_7_q), .clk(Clock));  // open: clr
  Register #(.width(32)) register_8 (
    .D(demultiplexer_1_out7), .en(ER7_out), .Q(register_8_q), .clk(Clock));  // open: clr
  Demultiplexer #(.select(4), .width(32)) demultiplexer_1 (
    .out0(demultiplexer_1_out0), .out1(demultiplexer_1_out1), .out2(demultiplexer_1_out2),
    .out3(demultiplexer_1_out3), .out4(demultiplexer_1_out4), .out5(demultiplexer_1_out5),
    .out6(demultiplexer_1_out6), .out7(demultiplexer_1_out7), .out8(demultiplexer_1_out8),
    .out9(demultiplexer_1_out9), .out10(demultiplexer_1_out10), .out11(demultiplexer_1_out11),
    .out12(demultiplexer_1_out12), .out13(demultiplexer_1_out13), .out14(demultiplexer_1_out14),
    .out15(demultiplexer_1_out15), .in(Data), .sel(SetRegister));
  Register #(.width(32)) register_9 (
    .D(demultiplexer_1_out8), .en(ER8_out), .Q(register_9_q), .clk(Clock));  // open: clr
  Register #(.width(32)) register_10 (
    .D(demultiplexer_1_out9), .en(ER9_out), .Q(register_10_q), .clk(Clock));  // open: clr
  Register #(.width(32)) register_11 (
    .D(demultiplexer_1_out10), .en(ER10_out), .Q(register_11_q), .clk(Clock));  // open: clr
  Register #(.width(32)) register_12 (
    .D(demultiplexer_1_out11), .en(ER11_out), .Q(register_12_q), .clk(Clock));  // open: clr
  Register #(.width(32)) register_13 (
    .D(demultiplexer_1_out12), .en(ER12_out), .Q(register_13_q), .clk(Clock));  // open: clr
  Register #(.width(32)) register_14 (
    .D(demultiplexer_1_out13), .en(ER13_out), .Q(register_14_q), .clk(Clock));  // open: clr
  Register #(.width(32)) register_15 (
    .D(demultiplexer_1_out14), .en(ER14_out), .Q(register_15_q), .clk(Clock));  // open: clr
  Register #(.width(32)) register_16 (
    .D(demultiplexer_1_out15), .en(ER15_out), .Q(register_16_q), .clk(Clock));  // open: clr
  Multiplexer #(.enable("true"), .select(4), .width(32)) multiplexer_1 (
    .in0(register_1_q), .in1(register_2_q), .in2(register_3_q), .in3(register_4_q), .in4(register_5_q),
    .in5(register_6_q), .in6(register_7_q), .in7(register_8_q), .in8(register_9_q), .in9(register_10_q),
    .in10(register_11_q), .in11(register_12_q), .in12(register_13_q), .in13(register_14_q),
    .in14(register_15_q), .in15(register_16_q), .out(OutputY), .sel(ReadRegisterY), .en(EnableRead));
  Multiplexer #(.enable("true"), .select(4), .width(32)) multiplexer_2 (
    .in0(register_1_q), .in1(register_2_q), .in2(register_3_q), .in3(register_4_q), .in4(register_5_q),
    .in5(register_6_q), .in6(register_7_q), .in7(register_8_q), .in8(register_9_q), .in9(register_10_q),
    .in10(register_11_q), .in11(register_12_q), .in12(register_13_q), .in13(register_14_q),
    .in14(register_15_q), .in15(register_16_q), .out(OutputX), .sel(ReadRegisterX), .en(EnableRead));
endmodule

module fp_register_file (
);

  Register #(.width(32)) register_1 ();  // open: D, en, clk, Q, clr
  Register #(.width(32)) register_2 ();  // open: D, en, clk, Q, clr
  Register #(.width(32)) register_3 ();  // open: D, en, clk, Q, clr
  Register #(.width(32)) register_4 ();  // open: D, en, clk, Q, clr
  Register #(.width(32)) register_5 ();  // open: D, en, clk, Q, clr
  Register #(.width(32)) register_6 ();  // open: D, en, clk, Q, clr
  Register #(.width(32)) register_7 ();  // open: D, en, clk, Q, clr
  Register #(.width(32)) register_8 ();  // open: D, en, clk, Q, clr
  Register #(.width(32)) register_9 ();  // open: D, en, clk, Q, clr
  Register #(.width(32)) register_10 ();  // open: D, en, clk, Q, clr
  Register #(.width(32)) register_11 ();  // open: D, en, clk, Q, clr
  Register #(.width(32)) register_12 ();  // open: D, en, clk, Q, clr
endmodule

module vector_register_file (
  input  [31:0] inputA0,
  input  [31:0] inputA1,
  input  [31:0] inputA2,
  input  [31:0] inputB0,
  input  [31:0] inputB1,
  input  in_6,
  input  [31:0] inputB2,
  input  EnableWrite1,
  input  EnableWrite2,
  input  [3:0] WriteToResgisterX,
  input  [3:0] WriteToRegisterY,
  input  ClearEnableX,
  input  ClearEnableY,
  input  [3:0] ClearRegisterX,
  input  [3:0] RegisterToReadX,
  input  [3:0] ClearRegisterY,
  input  [3:0] RegisterToReadY,
  output [31:0] X0,
  output [31:0] X1,
  output [31:0] X2,
  output [31:0] Y0,
  output [31:0] Y2,
  output [31:0] Y3
);

  wire ReadEnableController_output0, ReadEnableController_output1, ReadEnableController_output2,
       ReadEnableController_output3, ReadEnableController_output4, ReadEnableController_output5,
       ReadEnableController_output6, ReadEnableController_output7, ReadEnableController_output8,
       ReadEnableController_output9, ReadEnableController_output10, ReadEnableController_output11,
       ReadEnableController_output12, ReadEnableController_output13, ReadEnableController_output14,
       ReadEnableController_output15, WriteEnableController_output0, WriteEnableController_output1,
       WriteEnableController_output2, WriteEnableController_output3, WriteEnableController_output4,
       WriteEnableController_output5, WriteEnableController_output6, WriteEnableController_output7,
       WriteEnableController_output8, WriteEnableController_output9, WriteEnableController_output10,
       WriteEnableController_output11, WriteEnableController_output12, WriteEnableController_output13,
       WriteEnableController_output14, WriteEnableController_output15;
  wire [31:0] V0_output_0, V0_output_1, V0_output_2, V1_output_0, V1_output_1, V1_output_2, V2_output_0,
       V2_output_1, V2_output_2, V3_output_0, V3_output_1, V3_output_2, V4_output_0, V4_output_1,
       V4_output_2, V5_output_0, V5_output_1, V5_output_2, V6_output_0, V6_output_1, V6_output_2,
       V7_output_0, V7_output_1, V7_output_2, V8_output_0, V8_output_1, V8_output_2, V9_output_0,
       V9_output_1, V9_output_2, V10_output_0, V10_output_1, V10_output_2, V11_output_0, V11_output_1,
       V11_output_2, V12_output_0, V12_output_1, V12_output_2, V13_output_0, V13_output_1, V13_output_2,
       V14_output_0, V14_output_1, V14_output_2, V15_output_0, V15_output_1, V15_output_2,
       vr_write_controller_1_data1, vr_write_controller_1_data2, vr_write_controller_1_data3,
       vr_write_controller_2_data1, vr_write_controller_2_data2, vr_write_controller_2_data3,
       vr_write_controller_3_data1, vr_write_controller_3_data2, vr_write_controller_3_data3,
       vr_write_controller_4_data1, vr_write_controller_4_data2, vr_write_controller_4_data3,
       vr_write_controller_5_data1, vr_write_controller_5_data2, vr_write_controller_5_data3,
       vr_write_controller_6_data1, vr_write_controller_6_data2, vr_write_controller_6_data3,
       vr_write_controller_7_data1, vr_write_controller_7_data2, vr_write_controller_7_data3,
       vr_write_controller_8_data1, vr_write_controller_8_data2, vr_write_controller_8_data3,
       vr_write_controller_9_data1, vr_write_controller_9_data2, vr_write_controller_9_data3,
       vr_write_controller_10_data1, vr_write_controller_10_data2, vr_write_controller_10_data3,
       vr_write_controller_11_data1, vr_write_controller_11_data2, vr_write_controller_11_data3,
       vr_write_controller_12_data1, vr_write_controller_12_data2, vr_write_controller_12_data3,
       vr_write_controller_13_data1, vr_write_controller_13_data2, vr_write_controller_13_data3,
       vr_write_controller_14_data1, vr_write_controller_14_data2, vr_write_controller_14_data3,
       vr_write_controller_15_data1, vr_write_controller_15_data2, vr_write_controller_15_data3,
       vr_write_controller_16_data1, vr_write_controller_16_data2, vr_write_controller_16_data3;

  double_demux WriteEnableController (
    .Select1(WriteToResgisterX), .Select2(WriteToRegisterY), .Input1(EnableWrite1), .Input2(EnableWrite2),
    .Output0(WriteEnableController_output0), .Output1(WriteEnableController_output1),
    .Output9(WriteEnableController_output9), .Output10(WriteEnableController_output10),
    .output11(WriteEnableController_output11), .Output12(WriteEnableController_output12),
    .Output13(WriteEnableController_output13), .Output2(WriteEnableController_output2),
    .Output3(WriteEnableController_output3), .Output4(WriteEnableController_output4),
    .Output5(WriteEnableController_output5), .Output6(WriteEnableController_output6),
    .Output7(WriteEnableController_output7), .OUtput8(WriteEnableController_output8),
    .Output14(WriteEnableController_output14), .Output15(WriteEnableController_output15));
  double_demux ReadEnableController (
    .Select1(ClearRegisterX), .Select2(ClearRegisterY), .Input1(ClearEnableX), .Input2(ClearEnableY),
    .Output0(ReadEnableController_output0), .Output1(ReadEnableController_output1),
    .Output9(ReadEnableController_output9), .Output10(ReadEnableController_output10),
    .output11(ReadEnableController_output11), .Output12(ReadEnableController_output12),
    .Output13(ReadEnableController_output13), .Output2(ReadEnableController_output2),
    .Output3(ReadEnableController_output3), .Output4(ReadEnableController_output4),
    .Output5(ReadEnableController_output5), .Output6(ReadEnableController_output6),
    .Output7(ReadEnableController_output7), .OUtput8(ReadEnableController_output8),
    .Output14(ReadEnableController_output14), .Output15(ReadEnableController_output15));
  vr_write_controller vr_write_controller_1 (
    .EnableFlow2(EnableWrite2), .enableFlow1(EnableWrite1), .dataA1(inputA0), .dataA2(inputA1),
    .dataA3(inputA2), .dataB1(inputB0), .dataB2(inputB1), .dataB3(inputB2),
    .data1(vr_write_controller_1_data1), .data2(vr_write_controller_1_data2),
    .data3(vr_write_controller_1_data3));
  vr_write_controller vr_write_controller_2 (
    .EnableFlow2(EnableWrite2), .enableFlow1(EnableWrite1), .dataA1(inputA0), .dataA2(inputA1),
    .dataA3(inputA2), .dataB1(inputB0), .dataB2(inputB1), .dataB3(inputB2),
    .data1(vr_write_controller_2_data1), .data2(vr_write_controller_2_data2),
    .data3(vr_write_controller_2_data3));
  vector_register V0 (
    .Clock(in_6), .WriteEnable(WriteEnableController_output0), .Clear(ReadEnableController_output0),
    .Input_0(vr_write_controller_1_data1), .Input_1(vr_write_controller_1_data2),
    .Input_2(vr_write_controller_1_data3), .Output_0(V0_output_0), .Output_1(V0_output_1),
    .Output_2(V0_output_2));
  vector_register V8 (
    .Clock(in_6), .WriteEnable(WriteEnableController_output8), .Clear(ReadEnableController_output8),
    .Input_0(vr_write_controller_2_data1), .Input_1(vr_write_controller_2_data2),
    .Input_2(vr_write_controller_2_data3), .Output_0(V8_output_0), .Output_1(V8_output_1),
    .Output_2(V8_output_2));
  vr_write_controller vr_write_controller_3 (
    .EnableFlow2(EnableWrite2), .enableFlow1(EnableWrite1), .dataA1(inputA0), .dataA2(inputA1),
    .dataA3(inputA2), .dataB1(inputB0), .dataB2(inputB1), .dataB3(inputB2),
    .data1(vr_write_controller_3_data1), .data2(vr_write_controller_3_data2),
    .data3(vr_write_controller_3_data3));
  vr_write_controller vr_write_controller_4 (
    .EnableFlow2(EnableWrite2), .enableFlow1(EnableWrite1), .dataA1(inputA0), .dataA2(inputA1),
    .dataA3(inputA2), .dataB1(inputB0), .dataB2(inputB1), .dataB3(inputB2),
    .data1(vr_write_controller_4_data1), .data2(vr_write_controller_4_data2),
    .data3(vr_write_controller_4_data3));
  vector_register V9 (
    .Clock(in_6), .WriteEnable(WriteEnableController_output9), .Clear(ReadEnableController_output9),
    .Input_0(vr_write_controller_4_data1), .Input_1(vr_write_controller_4_data2),
    .Input_2(vr_write_controller_4_data3), .Output_0(V9_output_0), .Output_1(V9_output_1),
    .Output_2(V9_output_2));
  vector_register V1 (
    .Clock(in_6), .WriteEnable(WriteEnableController_output1), .Clear(ReadEnableController_output1),
    .Input_0(vr_write_controller_3_data1), .Input_1(vr_write_controller_3_data2),
    .Input_2(vr_write_controller_3_data3), .Output_0(V1_output_0), .Output_1(V1_output_1),
    .Output_2(V1_output_2));
  vr_write_controller vr_write_controller_5 (
    .EnableFlow2(EnableWrite2), .enableFlow1(EnableWrite1), .dataA1(inputA0), .dataA2(inputA1),
    .dataA3(inputA2), .dataB1(inputB0), .dataB2(inputB1), .dataB3(inputB2),
    .data1(vr_write_controller_5_data1), .data2(vr_write_controller_5_data2),
    .data3(vr_write_controller_5_data3));
  vr_write_controller vr_write_controller_6 (
    .EnableFlow2(EnableWrite2), .enableFlow1(EnableWrite1), .dataA1(inputA0), .dataA2(inputA1),
    .dataA3(inputA2), .dataB1(inputB0), .dataB2(inputB1), .dataB3(inputB2),
    .data1(vr_write_controller_6_data1), .data2(vr_write_controller_6_data2),
    .data3(vr_write_controller_6_data3));
  vector_register V10 (
    .Clock(in_6), .WriteEnable(WriteEnableController_output10), .Clear(ReadEnableController_output10),
    .Input_0(vr_write_controller_6_data1), .Input_1(vr_write_controller_6_data2),
    .Input_2(vr_write_controller_6_data3), .Output_0(V10_output_0), .Output_1(V10_output_1),
    .Output_2(V10_output_2));
  vector_register V2 (
    .Clock(in_6), .WriteEnable(WriteEnableController_output2), .Clear(ReadEnableController_output2),
    .Input_0(vr_write_controller_5_data1), .Input_1(vr_write_controller_5_data2),
    .Input_2(vr_write_controller_5_data3), .Output_0(V2_output_0), .Output_1(V2_output_1),
    .Output_2(V2_output_2));
  vr_write_controller vr_write_controller_7 (
    .EnableFlow2(EnableWrite2), .enableFlow1(EnableWrite1), .dataA1(inputA0), .dataA2(inputA1),
    .dataA3(inputA2), .dataB1(inputB0), .dataB2(inputB1), .dataB3(inputB2),
    .data1(vr_write_controller_7_data1), .data2(vr_write_controller_7_data2),
    .data3(vr_write_controller_7_data3));
  vr_write_controller vr_write_controller_8 (
    .EnableFlow2(EnableWrite2), .enableFlow1(EnableWrite1), .dataA1(inputA0), .dataA2(inputA1),
    .dataA3(inputA2), .dataB1(inputB0), .dataB2(inputB1), .dataB3(inputB2),
    .data1(vr_write_controller_8_data1), .data2(vr_write_controller_8_data2),
    .data3(vr_write_controller_8_data3));
  vector_register V11 (
    .Clock(in_6), .WriteEnable(WriteEnableController_output11), .Clear(ReadEnableController_output11),
    .Input_0(vr_write_controller_7_data1), .Input_1(vr_write_controller_7_data2),
    .Input_2(vr_write_controller_7_data3), .Output_0(V11_output_0), .Output_1(V11_output_1),
    .Output_2(V11_output_2));
  vector_register V3 (
    .Clock(in_6), .WriteEnable(WriteEnableController_output3), .Clear(ReadEnableController_output3),
    .Input_0(vr_write_controller_8_data1), .Input_1(vr_write_controller_8_data2),
    .Input_2(vr_write_controller_8_data3), .Output_0(V3_output_0), .Output_1(V3_output_1),
    .Output_2(V3_output_2));
  vr_write_controller vr_write_controller_9 (
    .EnableFlow2(EnableWrite2), .enableFlow1(EnableWrite1), .dataA1(inputA0), .dataA2(inputA1),
    .dataA3(inputA2), .dataB1(inputB0), .dataB2(inputB1), .dataB3(inputB2),
    .data1(vr_write_controller_9_data1), .data2(vr_write_controller_9_data2),
    .data3(vr_write_controller_9_data3));
  vr_write_controller vr_write_controller_10 (
    .EnableFlow2(EnableWrite2), .enableFlow1(EnableWrite1), .dataA1(inputA0), .dataA2(inputA1),
    .dataA3(inputA2), .dataB1(inputB0), .dataB2(inputB1), .dataB3(inputB2),
    .data1(vr_write_controller_10_data1), .data2(vr_write_controller_10_data2),
    .data3(vr_write_controller_10_data3));
  vector_register V12 (
    .Clock(in_6), .WriteEnable(WriteEnableController_output12), .Clear(ReadEnableController_output12),
    .Input_0(vr_write_controller_9_data1), .Input_1(vr_write_controller_9_data2),
    .Input_2(vr_write_controller_9_data3), .Output_0(V12_output_0), .Output_1(V12_output_1),
    .Output_2(V12_output_2));
  vector_register V4 (
    .Clock(in_6), .WriteEnable(WriteEnableController_output4), .Clear(ReadEnableController_output4),
    .Input_0(vr_write_controller_10_data1), .Input_1(vr_write_controller_10_data2),
    .Input_2(vr_write_controller_10_data3), .Output_0(V4_output_0), .Output_1(V4_output_1),
    .Output_2(V4_output_2));
  vr_write_controller vr_write_controller_11 (
    .EnableFlow2(EnableWrite2), .enableFlow1(EnableWrite1), .dataA1(inputA0), .dataA2(inputA1),
    .dataA3(inputA2), .dataB1(inputB0), .dataB2(inputB1), .dataB3(inputB2),
    .data1(vr_write_controller_11_data1), .data2(vr_write_controller_11_data2),
    .data3(vr_write_controller_11_data3));
  vr_write_controller vr_write_controller_12 (
    .EnableFlow2(EnableWrite2), .enableFlow1(EnableWrite1), .dataA1(inputA0), .dataA2(inputA1),
    .dataA3(inputA2), .dataB1(inputB0), .dataB2(inputB1), .dataB3(inputB2),
    .data1(vr_write_controller_12_data1), .data2(vr_write_controller_12_data2),
    .data3(vr_write_controller_12_data3));
  vector_register V5 (
    .Clock(in_6), .WriteEnable(WriteEnableController_output5), .Clear(ReadEnableController_output5),
    .Input_0(vr_write_controller_12_data1), .Input_1(vr_write_controller_12_data2),
    .Input_2(vr_write_controller_12_data3), .Output_0(V5_output_0), .Output_1(V5_output_1),
    .Output_2(V5_output_2));
  vector_register V13 (
    .Clock(in_6), .WriteEnable(WriteEnableController_output13), .Clear(ReadEnableController_output13),
    .Input_0(vr_write_controller_11_data1), .Input_1(vr_write_controller_11_data2),
    .Input_2(vr_write_controller_11_data3), .Output_0(V13_output_0), .Output_1(V13_output_1),
    .Output_2(V13_output_2));
  vr_write_controller vr_write_controller_13 (
    .EnableFlow2(EnableWrite2), .enableFlow1(EnableWrite1), .dataA1(inputA0), .dataA2(inputA1),
    .dataA3(inputA2), .dataB1(inputB0), .dataB2(inputB1), .dataB3(inputB2),
    .data1(vr_write_controller_13_data1), .data2(vr_write_controller_13_data2),
    .data3(vr_write_controller_13_data3));
  vr_write_controller vr_write_controller_14 (
    .EnableFlow2(EnableWrite2), .enableFlow1(EnableWrite1), .dataA1(inputA0), .dataA2(inputA1),
    .dataA3(inputA2), .dataB1(inputB0), .dataB2(inputB1), .dataB3(inputB2),
    .data1(vr_write_controller_14_data1), .data2(vr_write_controller_14_data2),
    .data3(vr_write_controller_14_data3));
  vector_register V6 (
    .Clock(in_6), .WriteEnable(WriteEnableController_output6), .Clear(ReadEnableController_output6),
    .Input_0(vr_write_controller_14_data1), .Input_1(vr_write_controller_14_data2),
    .Input_2(vr_write_controller_14_data3), .Output_0(V6_output_0), .Output_1(V6_output_1),
    .Output_2(V6_output_2));
  vector_register V14 (
    .Clock(in_6), .WriteEnable(WriteEnableController_output14), .Clear(ReadEnableController_output14),
    .Input_0(vr_write_controller_13_data1), .Input_1(vr_write_controller_13_data2),
    .Input_2(vr_write_controller_13_data3), .Output_0(V14_output_0), .Output_1(V14_output_1),
    .Output_2(V14_output_2));
  vr_write_controller vr_write_controller_15 (
    .EnableFlow2(EnableWrite2), .enableFlow1(EnableWrite1), .dataA1(inputA0), .dataA2(inputA1),
    .dataA3(inputA2), .dataB1(inputB0), .dataB2(inputB1), .dataB3(inputB2),
    .data1(vr_write_controller_15_data1), .data2(vr_write_controller_15_data2),
    .data3(vr_write_controller_15_data3));
  vr_write_controller vr_write_controller_16 (
    .EnableFlow2(EnableWrite2), .enableFlow1(EnableWrite1), .dataA1(inputA0), .dataA2(inputA1),
    .dataA3(inputA2), .dataB1(inputB0), .dataB2(inputB1), .dataB3(inputB2),
    .data1(vr_write_controller_16_data1), .data2(vr_write_controller_16_data2),
    .data3(vr_write_controller_16_data3));
  vector_register V7 (
    .Clock(in_6), .WriteEnable(WriteEnableController_output7), .Clear(ReadEnableController_output7),
    .Input_0(vr_write_controller_15_data1), .Input_1(vr_write_controller_15_data2),
    .Input_2(vr_write_controller_15_data3), .Output_0(V7_output_0), .Output_1(V7_output_1),
    .Output_2(V7_output_2));
  vector_register V15 (
    .Clock(in_6), .WriteEnable(WriteEnableController_output15), .Clear(ReadEnableController_output15),
    .Input_0(vr_write_controller_16_data1), .Input_1(vr_write_controller_16_data2),
    .Input_2(vr_write_controller_16_data3), .Output_0(V15_output_0), .Output_1(V15_output_1),
    .Output_2(V15_output_2));
  vector_mux vector_mux_1 (
    .input61(V6_output_1), .input62(V6_output_2), .input00(V0_output_0), .input70(V7_output_0),
    .input71(V7_output_1), .input72(V7_output_2), .input80(V8_output_0), .input81(V8_output_1),
    .input82(V8_output_2), .input90(V9_output_0), .input91(V9_output_1), .input92(V9_output_2),
    .input01(V0_output_1), .input100(V10_output_0), .input101(V10_output_1), .input102(V10_output_2),
    .input110(V11_output_0), .input111(V11_output_1), .input112(V11_output_2), .input120(V12_output_0),
    .input121(V12_output_1), .input02(V0_output_2), .input122(V12_output_2), .input130(V13_output_0),
    .input131(V13_output_1), .input132(V13_output_2), .input140(V14_output_0), .input141(V14_output_1),
    .input142(V14_output_2), .input150(V15_output_0), .input151(V15_output_1), .input152(V15_output_2),
    .input10(V1_output_0), .input11(V1_output_1), .input12(V1_output_2), .input20(V2_output_0),
    .input21(V2_output_1), .input22(V2_output_2), .input30(V3_output_0), .input31(V3_output_1),
    .input32(V3_output_2), .input40(V4_output_0), .input41(V4_output_1), .input42(V4_output_2),
    .input50(V5_output_0), .input51(V5_output_1), .input52(V5_output_2), .input60(V6_output_0),
    .selectBits(RegisterToReadX), .Output0(X0), .Output1(X1), .Output2(X2));
  vector_mux vector_mux_2 (
    .input61(V6_output_1), .input62(V6_output_2), .input00(V0_output_0), .input70(V7_output_0),
    .input71(V7_output_1), .input72(V7_output_2), .input80(V8_output_0), .input81(V8_output_1),
    .input82(V8_output_2), .input90(V9_output_0), .input91(V9_output_1), .input92(V9_output_2),
    .input01(V0_output_1), .input100(V10_output_0), .input101(V10_output_1), .input102(V10_output_2),
    .input110(V11_output_0), .input111(V11_output_1), .input112(V11_output_2), .input120(V12_output_0),
    .input121(V12_output_1), .input02(V0_output_2), .input122(V12_output_2), .input130(V13_output_0),
    .input131(V13_output_1), .input132(V13_output_2), .input140(V14_output_0), .input141(V14_output_1),
    .input142(V14_output_2), .input150(V15_output_0), .input151(V15_output_1), .input152(V15_output_2),
    .input10(V1_output_0), .input11(V1_output_1), .input12(V1_output_2), .input20(V2_output_0),
    .input21(V2_output_1), .input22(V2_output_2), .input30(V3_output_0), .input31(V3_output_1),
    .input32(V3_output_2), .input40(V4_output_0), .input41(V4_output_1), .input42(V4_output_2),
    .input50(V5_output_0), .input51(V5_output_1), .input52(V5_output_2), .input60(V6_output_0),
    .selectBits(RegisterToReadY), .Output0(Y0), .Output1(Y2), .Output2(Y3));
endmodule

module vector_register (
  input  WriteEnable,
  input  [31:0] Input_0,
  input  Clock,
  input  [31:0] Input_1,
  input  [31:0] Input_2,
  input  Clear,
  output [31:0] Output_0,
  output [31:0] Output_1,
  output [31:0] Output_2
);

  Register #(.width(32)) v_sub_0 (.D(Input_0), .en(WriteEnable), .clk(Clock), .Q(Output_0), .clr(Clear));
  Register #(.width(32)) v_sub_1 (.D(Input_1), .en(WriteEnable), .clk(Clock), .Q(Output_1), .clr(Clear));
  Register #(.width(32)) v_sub_2 (.D(Input_2), .en(WriteEnable), .clk(Clock), .Q(Output_2));  // open: clr
endmodule

module double_demux (
  input  [3:0] Select1,
  input  [3:0] Select2,
  input  Input2,
  input  Input1,
  output Output0,
  output Output1,
  output Output2,
  output Output3,
  output Output4,
  output Output5,
  output Output6,
  output Output7,
  output OUtput8,
  output Output9,
  output Output10,
  output output11,
  output Output12,
  output Output13,
  output Output14,
  output Output15
);

  wire demultiplexer_1_out0, demultiplexer_1_out1, demultiplexer_1_out2, demultiplexer_1_out3,
       demultiplexer_1_out4, demultiplexer_1_out5, demultiplexer_1_out6, demultiplexer_1_out7,
       demultiplexer_1_out8, demultiplexer_1_out9, demultiplexer_1_out10, demultiplexer_1_out11,
       demultiplexer_1_out12, demultiplexer_1_out13, demultiplexer_1_out14, demultiplexer_1_out15,
       demultiplexer_2_out0, demultiplexer_2_out1, demultiplexer_2_out2, demultiplexer_2_out3,
       demultiplexer_2_out4, demultiplexer_2_out5, demultiplexer_2_out6, demultiplexer_2_out7,
       demultiplexer_2_out8, demultiplexer_2_out9, demultiplexer_2_out10, demultiplexer_2_out11,
       demultiplexer_2_out12, demultiplexer_2_out13, demultiplexer_2_out14, demultiplexer_2_out15;

  Demultiplexer #(.select(4)) demultiplexer_1 (
    .out0(demultiplexer_1_out0), .out1(demultiplexer_1_out1), .out2(demultiplexer_1_out2),
    .out3(demultiplexer_1_out3), .out4(demultiplexer_1_out4), .out5(demultiplexer_1_out5),
    .out6(demultiplexer_1_out6), .out7(demultiplexer_1_out7), .out8(demultiplexer_1_out8),
    .out9(demultiplexer_1_out9), .out10(demultiplexer_1_out10), .out11(demultiplexer_1_out11),
    .out12(demultiplexer_1_out12), .out13(demultiplexer_1_out13), .out14(demultiplexer_1_out14),
    .out15(demultiplexer_1_out15), .in(Input1), .sel(Select1));
  Demultiplexer #(.select(4)) demultiplexer_2 (
    .out0(demultiplexer_2_out0), .out1(demultiplexer_2_out1), .out2(demultiplexer_2_out2),
    .out3(demultiplexer_2_out3), .out4(demultiplexer_2_out4), .out5(demultiplexer_2_out5),
    .out6(demultiplexer_2_out6), .out7(demultiplexer_2_out7), .out8(demultiplexer_2_out8),
    .out9(demultiplexer_2_out9), .out10(demultiplexer_2_out10), .out11(demultiplexer_2_out11),
    .out12(demultiplexer_2_out12), .out13(demultiplexer_2_out13), .out14(demultiplexer_2_out14),
    .out15(demultiplexer_2_out15), .in(Input2), .sel(Select2));
  or or_1 (Output0, demultiplexer_1_out0, demultiplexer_2_out0);
  or or_2 (Output1, demultiplexer_1_out1, demultiplexer_2_out1);
  or or_3 (Output2, demultiplexer_1_out2, demultiplexer_2_out2);
  or or_4 (Output3, demultiplexer_1_out3, demultiplexer_2_out3);
  or or_5 (Output4, demultiplexer_1_out4, demultiplexer_2_out4);
  or or_6 (Output5, demultiplexer_1_out5, demultiplexer_2_out5);
  or or_7 (Output6, demultiplexer_1_out6, demultiplexer_2_out6);
  or or_8 (Output7, demultiplexer_1_out7, demultiplexer_2_out7);
  or or_9 (OUtput8, demultiplexer_1_out8, demultiplexer_2_out8);
  or or_10 (Output9, demultiplexer_1_out9, demultiplexer_2_out9);
  or or_11 (Output10, demultiplexer_1_out10, demultiplexer_2_out10);
  or or_12 (output11, demultiplexer_1_out11, demultiplexer_2_out11);
  or or_13 (Output12, demultiplexer_1_out12, demultiplexer_2_out12);
  or or_14 (Output13, demultiplexer_1_out13, demultiplexer_2_out13);
  or or_15 (Output14, demultiplexer_1_out14, demultiplexer_2_out14);
  or or_16 (Output15, demultiplexer_1_out15, demultiplexer_2_out15);
endmodule

module vector_mux (
  input  [31:0] input00,
  input  [31:0] input01,
  input  [31:0] input02,
  input  [31:0] input10,
  input  [31:0] input11,
  input  [31:0] input12,
  input  [31:0] input20,
  input  [31:0] input21,
  input  [31:0] input22,
  input  [31:0] input30,
  input  [31:0] input31,
  input  [31:0] input32,
  input  [31:0] input40,
  input  [31:0] input41,
  input  [31:0] input42,
  input  [31:0] input50,
  input  [31:0] input51,
  input  [31:0] input52,
  input  [31:0] input60,
  input  [31:0] input61,
  input  [31:0] input62,
  input  [31:0] input70,
  input  [31:0] input71,
  input  [31:0] input72,
  input  [31:0] input80,
  input  [31:0] input81,
  input  [31:0] input82,
  input  [31:0] input90,
  input  [31:0] input91,
  input  [31:0] input92,
  input  [31:0] input100,
  input  [31:0] input101,
  input  [31:0] input102,
  input  [31:0] input110,
  input  [31:0] input111,
  input  [31:0] input112,
  input  [31:0] input120,
  input  [31:0] input121,
  input  [31:0] input122,
  input  [31:0] input130,
  input  [31:0] input131,
  input  [31:0] input132,
  input  [31:0] input140,
  input  [31:0] input141,
  input  [31:0] input142,
  input  [31:0] input150,
  input  [31:0] input151,
  input  [31:0] input152,
  input  [3:0] selectBits,
  output [31:0] Output0,
  output [31:0] Output1,
  output [31:0] Output2
);

  Multiplexer #(.select(4), .width(32)) multiplexer_1 (
    .in0(input00), .in1(input10), .in2(input20), .in3(input30), .in4(input40), .in5(input50), .in6(input60),
    .in7(input70), .in8(input80), .in9(input90), .in10(input100), .in11(input110), .in12(input120),
    .in13(input130), .in14(input140), .in15(input150), .out(Output0), .sel(selectBits));
  Multiplexer #(.select(4), .width(32)) multiplexer_2 (
    .in0(input01), .in1(input11), .in2(input21), .in3(input31), .in4(input41), .in5(input51), .in6(input61),
    .in7(input71), .in8(input81), .in9(input91), .in10(input101), .in11(input111), .in12(input121),
    .in13(input131), .in14(input141), .in15(input151), .out(Output1), .sel(selectBits));
  Multiplexer #(.select(4), .width(32)) multiplexer_3 (
    .in0(input02), .in1(input12), .in2(input22), .in3(input32), .in4(input42), .in5(input52), .in6(input62),
    .in7(input72), .in8(input82), .in9(input92), .in10(input102), .in11(input112), .in12(input122),
    .in13(input132), .in14(input142), .in15(input152), .out(Output2), .sel(selectBits));
endmodule

module vr_write_sub_controller (
  input  [31:0] inputA,
  input  [31:0] InputB,
  input  enableFlow1,
  input  enableFlow2,
  output [31:0] data
);

  wire and_1_out;

  and and_1 (and_1_out, ~enableFlow1, enableFlow2);  // AND_Gate
  Multiplexer #(.width(32)) multiplexer_1 (.in0(inputA), .in1(InputB), .out(data), .sel(and_1_out));
endmodule

module vr_write_controller (
  input  [31:0] dataA1,
  input  [31:0] dataA2,
  input  [31:0] dataA3,
  input  [31:0] dataB1,
  input  [31:0] dataB2,
  input  [31:0] dataB3,
  input  enableFlow1,
  input  EnableFlow2,
  output [31:0] data1,
  output [31:0] data2,
  output [31:0] data3
);

  vr_write_sub_controller vr_write_sub_controller_1 (
    .enableFlow1(enableFlow1), .enableFlow2(EnableFlow2), .inputA(dataA1), .InputB(dataB1), .data(data1));
  vr_write_sub_controller vr_write_sub_controller_2 (
    .enableFlow1(enableFlow1), .enableFlow2(EnableFlow2), .inputA(dataA2), .InputB(dataB2), .data(data2));
  vr_write_sub_controller vr_write_sub_controller_3 (
    .enableFlow1(enableFlow1), .enableFlow2(EnableFlow2), .inputA(dataA3), .InputB(dataB3), .data(data3));
endmodule

module int_instruction_identifier (
  input  [31:0] in_1,
  input  [31:0] in_2,
  output [6:0] opcode,
  output [4:0] rd,
  output [2:0] funct3,
  output [4:0] rs1,
  output [4:0] rs2,
  output [6:0] funct7,
  output [11:0] inmm110,
  output [4:0] imm40,
  output [6:0] imm115,
  output imm11,
  output [3:0] imm41,
  output [5:0] imm105,
  output imm12,
  output [19:0] imm3112,
  output [7:0] imm1912,
  output imm112,
  output [9:0] imm101,
  output imm20
);

  int_opcode_identifier int_opcode_identifier_1 ();  // open: Opcode, IsIntOperation
  int_funct7_identifier int_funct7_identifier_1 ();  // open: Funct7, IsIntFunct7
  int_funct3_identifier int_funct3_identifier_1 ();  // open: Funct3, IsIntFunct3

  assign funct3 = in_1[14:12];
  assign funct7 = in_1[31:25];
  assign imm11 = in_1[7];
  assign imm12 = in_1[31];
  assign imm20 = in_1[31];
  assign imm40 = in_1[11:7];
  assign imm41 = in_1[11:8];
  assign imm101 = in_1[30:21];
  assign imm105 = in_1[30:25];
  assign imm112 = in_1[20];
  assign imm115 = in_1[31:25];
  assign imm1912 = in_1[19:12];
  assign imm3112 = in_1[31:12];
  assign inmm110 = in_1[31:20];
  assign opcode = in_1[6:0];
  assign rd = in_1[11:7];
  assign rs1 = in_1[19:15];
  assign rs2 = in_1[24:20];

  // Notes on the sheet:
  //   R-Type
  //   I-Type
  //   S-Type
  //   B-Type
  //   U-Type
  //   J-Type
  //   R-Type
  //   I-Type
  //   S-Type
  //   B-Type
  //   B-Type
  //   U-Type
  //   J-Type
endmodule

module int_opcode_identifier (
  input  [6:0] Opcode,
  output IsIntOperation
);

  wire ALI_out, ALR_out, AUIPC_out, BRANCH_out, ECB_out, FENCE_out, JAL_out, JALR_out, LOAD_out, LUI_out,
       STORE_out;

  and LUI (LUI_out, Opcode[0], Opcode[1], Opcode[2], ~Opcode[3], Opcode[4], Opcode[5], ~Opcode[6]);  // AND_Gate
  and AUIPC (AUIPC_out, Opcode[0], Opcode[1], Opcode[2], ~Opcode[3], Opcode[4], ~Opcode[5], ~Opcode[6]);  // AND_Gate
  and JAL (JAL_out, Opcode[0], Opcode[1], Opcode[2], Opcode[3], ~Opcode[4], Opcode[5], Opcode[6]);  // AND_Gate
  and JALR (JALR_out, Opcode[0], Opcode[1], Opcode[2], ~Opcode[3], ~Opcode[4], Opcode[5], Opcode[6]);  // AND_Gate
  and BRANCH (BRANCH_out, Opcode[0], Opcode[1], ~Opcode[2], ~Opcode[3], ~Opcode[4], Opcode[5], Opcode[6]);  // AND_Gate
  and LOAD (LOAD_out, Opcode[0], Opcode[1], ~Opcode[2], ~Opcode[3], ~Opcode[4], ~Opcode[5], ~Opcode[6]);  // AND_Gate
  and STORE (STORE_out, Opcode[0], Opcode[1], ~Opcode[2], ~Opcode[3], ~Opcode[4], Opcode[5], ~Opcode[6]);  // AND_Gate
  and ALI (ALI_out, Opcode[0], Opcode[1], ~Opcode[2], ~Opcode[3], Opcode[4], ~Opcode[5], ~Opcode[6]);  // AND_Gate
  and ALR (ALR_out, Opcode[0], Opcode[1], ~Opcode[2], ~Opcode[3], Opcode[4], Opcode[5], ~Opcode[6]);  // AND_Gate
  and FENCE (FENCE_out, Opcode[0], Opcode[1], Opcode[2], Opcode[3], ~Opcode[4], ~Opcode[5], ~Opcode[6]);  // AND_Gate
  and ECB (ECB_out, Opcode[0], Opcode[1], ~Opcode[2], ~Opcode[3], Opcode[4], Opcode[5], Opcode[6]);  // AND_Gate
  or or_1 (IsIntOperation, LUI_out, AUIPC_out, JAL_out, JALR_out, BRANCH_out, LOAD_out, STORE_out, ALI_out, ALR_out, FENCE_out, ECB_out);

  // Notes on the sheet:
  //   Arithmetic-Logic operation with Immediate
  //   Arithmetic-Logic operations with register
  //   I
  //   S
  //   I
  //   R
endmodule

module int_funct3_identifier (
  input  [2:0] Funct3,
  output IsIntFunct3
);

  wire and_1_out, and_2_out, and_3_out, and_4_out, and_5_out, and_6_out, and_7_out, and_8_out;

  and and_1 (and_1_out, ~Funct3[0], ~Funct3[1], ~Funct3[2]);  // AND_Gate
  and and_2 (and_2_out, Funct3[0], ~Funct3[1], ~Funct3[2]);  // AND_Gate
  and and_3 (and_3_out, ~Funct3[0], Funct3[1], ~Funct3[2]);  // AND_Gate
  and and_4 (and_4_out, Funct3[0], Funct3[1], ~Funct3[2]);  // AND_Gate
  and and_5 (and_5_out, ~Funct3[0], ~Funct3[1], Funct3[2]);  // AND_Gate
  and and_6 (and_6_out, Funct3[0], ~Funct3[1], Funct3[2]);  // AND_Gate
  and and_7 (and_7_out, ~Funct3[0], Funct3[1], Funct3[2]);  // AND_Gate
  and and_8 (and_8_out, Funct3[0], Funct3[1], Funct3[2]);
  or or_1 (IsIntFunct3, and_1_out, and_2_out, and_3_out, and_4_out, and_5_out, and_6_out, and_7_out, and_8_out);

  // Notes on the sheet:
  //   JALR - BEQ - LB - SB - ADDI - ADD - SUB-  FENCE - ECALL - EBREAK - MUL
  //   BNE - LH - SH -SLLI - SLL - MULH
  //   LW - SW - SLTI - SLT - MULHSU
  //   SLTIU - SLTU - MULHU
  //   BLT - LBU - XORI - XOR - DIV
  //   BGE - LHU - SRLI - SRAI - SRL -SRA - DIVU
  //   BLTU - ORI - OR - REM
  //   BGEU - ANDI - AND - REMU
endmodule

module int_funct7_identifier (
  input  [6:0] Funct7,
  output IsIntFunct7
);

  wire and_1_out, and_2_out, and_3_out, and_4_out, and_5_out;

  and and_1 (and_1_out, ~Funct7[0], ~Funct7[1], ~Funct7[2], ~Funct7[3], ~Funct7[4], ~Funct7[5], ~Funct7[6]);  // AND_Gate
  and and_2 (and_2_out, ~Funct7[0], ~Funct7[1], ~Funct7[2], ~Funct7[3], ~Funct7[4], Funct7[5], ~Funct7[6]);  // AND_Gate
  and and_3 (and_3_out, Funct7[0], ~Funct7[1], ~Funct7[2], ~Funct7[3], ~Funct7[4], ~Funct7[5], ~Funct7[6]);  // AND_Gate
  and and_4 (and_4_out, ~Funct7[0], ~Funct7[1], ~Funct7[2], Funct7[3], ~Funct7[4], ~Funct7[5], ~Funct7[6]);  // AND_Gate
  and and_5 (and_5_out, ~Funct7[0], ~Funct7[1], ~Funct7[2], Funct7[3], Funct7[4], ~Funct7[5], ~Funct7[6]);  // AND_Gate
  or or_1 (IsIntFunct7, and_1_out, and_2_out, and_3_out, and_4_out, and_5_out);

  // Notes on the sheet:
  //   SRAI - SUB -SRA
  //   MUL - MULH - MULHSU - MULHSU - MULHU - DIV - DIVU - REM - REMU
  //   SRET - WFI
  //   MRET
  //   SLLI - SRLI - ADD - SLL - SLT - SLTU - XOR - SRL - OR - AND
endmodule

// VHDL entity float_opcode_identifier, as the project stores it:
--------------------------------------------------------------------------------
-- Project :
-- File    :
-- Autor   :
-- Date    :
--
--------------------------------------------------------------------------------
-- Description :
--
--------------------------------------------------------------------------------

LIBRARY ieee;
USE ieee.std_logic_1164.ALL;

ENTITY float_opcode_identifier IS
    PORT (
        -- Input ports
        b1, b2, b3, b4, b5, b6, b7 : IN STD_LOGIC;
        -- Output ports
        is_valid : OUT STD_LOGIC
    );
END float_opcode_identifier;

--------------------------------------------------------------------------------
--Complete your VHDL description below
--------------------------------------------------------------------------------

ARCHITECTURE Identify OF float_opcode_identifier IS

BEGIN

    PROCESS (b1, b2, b3, b4, b5, b6, b7)
    BEGIN
        IF (b1 = '1' AND b2 = '1' AND b3 = '0' AND b4 = '0' AND b5 = '1' AND b6 = '0' AND b7 = '1') 
        OR (b1 = '1' AND b2 = '1' AND b3 = '1' AND b4 = '1' AND b5 = '0' AND b6 = '0' AND b7 = '1') 
        OR (b1 = '1' AND b2 = '1' AND b3 = '1' AND b4 = '0' AND b5 = '0' AND b6 = '0' AND b7 = '1') 
        OR (b1 = '1' AND b2 = '1' AND b3 = '0' AND b4 = '1' AND b5 = '0' AND b6 = '0' AND b7 = '1') 
        OR (b1 = '1' AND b2 = '1' AND b3 = '0' AND b4 = '0' AND b5 = '0' AND b6 = '0' AND b7 = '1') 
        OR (b1 = '1' AND b2 = '1' AND b3 = '1' AND b4 = '0' AND b5 = '0' AND b6 = '1' AND b7 = '0')
        OR (b1 = '1' AND b2 = '1' AND b3 = '1' AND b4 = '0' AND b5 = '0' AND b6 = '0' AND b7 = '0')  
        THEN
            is_valid <= '1';
        ELSE
            is_valid <= '0';
        END IF;
    END PROCESS;
END Identify;
